// Logisim project Project(main&bonus).circ as structural Verilog
module main (
);

  wire clock_1_out, dec_counter_1__0, dec_counter_1__1, dec_counter_1__2, dec_counter_1__3,
       simplification_mapped_1_a, simplification_mapped_1_b, simplification_mapped_1_c,
       simplification_mapped_1_d, simplification_mapped_1_e, simplification_mapped_1_f,
       simplification_mapped_1_g;

  Clock clock_1 (.out(clock_1_out));
  dec_counter dec_counter_1 (
    .Clock(clock_1_out), ._0(dec_counter_1__0), ._1(dec_counter_1__1), ._2(dec_counter_1__2),
    ._3(dec_counter_1__3));  // open: RESET
  simplification_mapped simplification_mapped_1 (
    .w(dec_counter_1__3), .x(dec_counter_1__2), .y(dec_counter_1__1), .z(dec_counter_1__0),
    .a(simplification_mapped_1_a), .b(simplification_mapped_1_b), .c(simplification_mapped_1_c),
    .d(simplification_mapped_1_d), .e(simplification_mapped_1_e), .f(simplification_mapped_1_f),
    .g(simplification_mapped_1_g));
  _7_Segment_Display u_7_segment_display_1 (
    .g(simplification_mapped_1_g), .f(simplification_mapped_1_f), .a(simplification_mapped_1_a),
    .b(simplification_mapped_1_b), .e(simplification_mapped_1_e), .d(simplification_mapped_1_d),
    .c(simplification_mapped_1_c));  // open: dp
endmodule

module bonus (
);

  wire and_1_out, clock_1_out, dec_counter_1__0, dec_counter_1__1, dec_counter_1__2, dec_counter_1__3,
       dec_counter_2__0, dec_counter_2__1, dec_counter_2__2, dec_counter_2__3, not_1_out, not_2_out,
       simplification_mapped_1_a, simplification_mapped_1_b, simplification_mapped_1_c,
       simplification_mapped_1_d, simplification_mapped_1_e, simplification_mapped_1_f,
       simplification_mapped_1_g, simplification_mapped_2_a, simplification_mapped_2_b,
       simplification_mapped_2_c, simplification_mapped_2_d, simplification_mapped_2_e,
       simplification_mapped_2_f, simplification_mapped_2_g;

  Clock clock_1 (.out(clock_1_out));
  dec_counter dec_counter_1 (
    .Clock(clock_1_out), ._0(dec_counter_1__0), ._1(dec_counter_1__1), ._2(dec_counter_1__2),
    ._3(dec_counter_1__3));  // open: RESET
  not not_1 (not_1_out, dec_counter_1__1);
  not not_2 (not_2_out, dec_counter_1__2);
  and and_1 (and_1_out, dec_counter_1__0, not_1_out, not_2_out, dec_counter_1__3);
  simplification_mapped simplification_mapped_1 (
    .w(dec_counter_1__3), .x(dec_counter_1__2), .y(dec_counter_1__1), .z(dec_counter_1__0),
    .a(simplification_mapped_1_a), .b(simplification_mapped_1_b), .c(simplification_mapped_1_c),
    .d(simplification_mapped_1_d), .e(simplification_mapped_1_e), .f(simplification_mapped_1_f),
    .g(simplification_mapped_1_g));
  simplification_mapped simplification_mapped_2 (
    .w(dec_counter_2__3), .x(dec_counter_2__2), .y(dec_counter_2__1), .z(dec_counter_2__0),
    .a(simplification_mapped_2_a), .b(simplification_mapped_2_b), .c(simplification_mapped_2_c),
    .d(simplification_mapped_2_d), .e(simplification_mapped_2_e), .f(simplification_mapped_2_f),
    .g(simplification_mapped_2_g));
  dec_counter dec_counter_2 (
    .Clock(and_1_out), ._0(dec_counter_2__0), ._1(dec_counter_2__1), ._2(dec_counter_2__2),
    ._3(dec_counter_2__3));  // open: RESET
  _7_Segment_Display u_7_segment_display_1 (
    .g(simplification_mapped_1_g), .f(simplification_mapped_1_f), .a(simplification_mapped_1_a),
    .b(simplification_mapped_1_b), .e(simplification_mapped_1_e), .d(simplification_mapped_1_d),
    .c(simplification_mapped_1_c));  // open: dp
  _7_Segment_Display u_7_segment_display_2 (
    .g(simplification_mapped_2_g), .f(simplification_mapped_2_f), .a(simplification_mapped_2_a),
    .b(simplification_mapped_2_b), .e(simplification_mapped_2_e), .d(simplification_mapped_2_d),
    .c(simplification_mapped_2_c));  // open: dp
endmodule

module dec_counter (
  input  Clock,
  output _0,
  output _1,
  output _2,
  output _3,
  output RESET
);

  wire and_2_out, and_3_out, and_4_out, and_5_out, and_6_out, and_7_out, and_8_out, D1_qn, D2_qn, D3_qn,
       D4_qn, or_1_out, or_2_out, or_3_out;

  and and_1 (RESET, _3, D2_qn, D3_qn, _0);
  and and_2 (and_2_out, _3, D4_qn);
  and and_3 (and_3_out, _2, _1, _0);
  and and_4 (and_4_out, _2, D3_qn);
  and and_5 (and_5_out, _2, D4_qn);
  and and_6 (and_6_out, D2_qn, _1, _0);
  and and_7 (and_7_out, _1, D4_qn);
  and and_8 (and_8_out, D1_qn, D3_qn, _0);
  or or_1 (or_1_out, and_2_out, and_3_out);
  or or_2 (or_2_out, and_4_out, and_5_out, and_6_out);
  or or_3 (or_3_out, and_7_out, and_8_out);
  D_Flip_Flop #(.trigger("falling")) D1 (.clk(Clock), .D(or_1_out), .Q(_3), .Qn(D1_qn));  // open: preset, en, reset
  D_Flip_Flop #(.trigger("falling")) D2 (.clk(Clock), .D(or_2_out), .Q(_2), .Qn(D2_qn));  // open: preset, en, reset
  D_Flip_Flop #(.trigger("falling")) D3 (.clk(Clock), .D(or_3_out), .Q(_1), .Qn(D3_qn));  // open: preset, en, reset
  D_Flip_Flop #(.trigger("falling")) D4 (.clk(Clock), .D(D4_qn), .Q(_0), .Qn(D4_qn));  // open: preset, en, reset
endmodule

module simplification_mapped (
  input  w,
  input  x,
  input  y,
  input  z,
  output a,
  output b,
  output c,
  output d,
  output e,
  output f,
  output g
);

  wire not_2_out, not_3_out, not_4_out, x_prime_y_2_out, x_prime_y_out, x_prime_z_prime_2_out,
       x_prime_z_prime_3_out, x_prime_z_prime_out, xy_prime_2_out, xy_prime_out, xy_prime_z_out, xz_out,
       xz_prime_out, y_prime_z_prime_2_out, y_prime_z_prime_out, yz_out, yz_prime_2_out, yz_prime_3_out,
       yz_prime_out;

  // NOT_Gate not_1 has open pins: in=w, out=open
  not not_2 (not_2_out, x);
  not not_3 (not_3_out, y);
  not not_4 (not_4_out, z);
  and xz (xz_out, z, x);
  and x_prime_z_prime (x_prime_z_prime_out, not_2_out, not_4_out);
  and y_prime_z_prime (y_prime_z_prime_out, not_4_out, not_3_out);
  and yz (yz_out, y, z);
  and x_prime_z_prime_2 (x_prime_z_prime_2_out, not_2_out, not_4_out);
  and x_prime_y (x_prime_y_out, not_2_out, y);
  and xy_prime_z (xy_prime_z_out, x, not_3_out, z);
  and yz_prime (yz_prime_out, y, not_4_out);
  and x_prime_z_prime_3 (x_prime_z_prime_3_out, not_2_out, not_4_out);
  and yz_prime_2 (yz_prime_2_out, y, not_4_out);
  and y_prime_z_prime_2 (y_prime_z_prime_2_out, not_3_out, not_4_out);
  and xy_prime (xy_prime_out, x, not_3_out);
  and xz_prime (xz_prime_out, x, not_4_out);
  and x_prime_y_2 (x_prime_y_2_out, not_2_out, y);
  and yz_prime_3 (yz_prime_3_out, y, not_4_out);
  and xy_prime_2 (xy_prime_2_out, x, not_3_out);
  or or_1 (a, xz_out, x_prime_z_prime_out, w, y);
  or or_2 (b, y_prime_z_prime_out, yz_out, not_2_out);
  or or_3 (c, x, not_3_out, z);
  or or_4 (d, x_prime_z_prime_2_out, x_prime_y_out, xy_prime_z_out, yz_prime_out, w);
  or or_5 (e, x_prime_z_prime_3_out, yz_prime_2_out);
  or or_6 (f, w, y_prime_z_prime_2_out, xy_prime_out, xz_prime_out);
  or or_7 (g, w, x_prime_y_2_out, yz_prime_3_out, xy_prime_2_out);
endmodule
